// Logisim project sattelite_prn_generation_using_Linear_Feedback_Shift_Register3.circ as structural Verilog: 1 circuit, main circuit main
module main (
  output out_1,
  output out_2
);

  wire adder_1_out, adder_2_out, adder_3_out, adder_4_out, adder_5_out, adder_6_out, adder_7_out,
       clock_1_out, counter_1_carry, counter_5_carry, counter_6_carry, counter_7_carry, odd_parity_1_out,
       shift_register_1_q0, shift_register_1_q1, shift_register_1_q2, shift_register_1_q3,
       shift_register_1_q4, shift_register_1_q5, shift_register_1_q6, shift_register_1_q7,
       shift_register_1_q8, shift_register_1_q9, shift_register_2_q2, shift_register_2_q9;
  wire [4:0] counter_2_q, counter_3_q, counter_4_q;
  wire [31:0] ram_1_data, ram_2_data, ram_3_data, shift_register_3_q31, shift_register_4_q31,
       shift_register_5_q31;

  Clock clock_1 (.out(clock_1_out));
  Counter #(.width(10), .max('h3ff)) counter_1 (
    .carry(counter_1_carry), .clk(clock_1_out));  // open: load, D, count, Q, clr
  Shift_Register #(.length(10)) shift_register_1 (
    .shift(clock_1_out), .in(odd_parity_1_out), .clk(clock_1_out), .out(out_2), .load(counter_1_carry),
    .d0(counter_1_carry), .q0(shift_register_1_q0), .d1(counter_1_carry), .q1(shift_register_1_q1),
    .d2(counter_1_carry), .q2(shift_register_1_q2), .d3(counter_1_carry), .q3(shift_register_1_q3),
    .d4(counter_1_carry), .q4(shift_register_1_q4), .d5(counter_1_carry), .q5(shift_register_1_q5),
    .d6(counter_1_carry), .q6(shift_register_1_q6), .d7(counter_1_carry), .q7(shift_register_1_q7),
    .d8(counter_1_carry), .q8(shift_register_1_q8), .d9(counter_1_carry), .q9(shift_register_1_q9));  // open: clr
  Shift_Register #(.length(10)) shift_register_2 (
    .shift(clock_1_out), .in(adder_4_out), .clk(clock_1_out), .out(out_1), .load(counter_1_carry),
    .d0(counter_1_carry), .d1(counter_1_carry), .d2(counter_1_carry), .q2(shift_register_2_q2),
    .d3(counter_1_carry), .d4(counter_1_carry), .d5(counter_1_carry), .d6(counter_1_carry),
    .d7(counter_1_carry), .d8(counter_1_carry), .d9(counter_1_carry), .q9(shift_register_2_q9));  // open: clr, q0, q1, q3, q4, q5, q6, q7, q8
  xor odd_parity_1 (odd_parity_1_out, shift_register_1_q1, shift_register_1_q2, shift_register_1_q5, shift_register_1_q7, shift_register_1_q8, shift_register_1_q9);
  Adder #(.width(1)) adder_1 (.a(shift_register_1_q1), .b(shift_register_1_q5), .out(adder_1_out));  // open: cin, cout
  Adder #(.width(1)) adder_2 (.a(shift_register_1_q7), .b(shift_register_1_q3), .out(adder_2_out));  // open: cin, cout
  Adder #(.width(1)) adder_3 (.a(shift_register_1_q1), .b(shift_register_1_q0), .out(adder_3_out));  // open: cin, cout
  Adder #(.width(1)) adder_4 (.a(shift_register_2_q9), .b(shift_register_2_q2), .out(adder_4_out));  // open: cin, cout
  Adder #(.width(1)) adder_5 (.a(out_1), .b(adder_1_out), .out(adder_5_out));  // open: cin, cout
  Adder #(.width(1)) adder_6 (.a(out_1), .b(adder_2_out), .out(adder_6_out));  // open: cin, cout
  Adder #(.width(1)) adder_7 (.a(out_1), .b(adder_3_out), .out(adder_7_out));  // open: cin, cout
  Shift_Register #(.length(32)) shift_register_3 (
    .shift(clock_1_out), .in(adder_5_out), .clk(clock_1_out), .q0(shift_register_3_q31[31]),
    .q1(shift_register_3_q31[30]), .q2(shift_register_3_q31[29]), .q3(shift_register_3_q31[28]),
    .q4(shift_register_3_q31[27]), .q5(shift_register_3_q31[26]), .q6(shift_register_3_q31[25]),
    .q7(shift_register_3_q31[24]), .q8(shift_register_3_q31[23]), .q9(shift_register_3_q31[22]),
    .q10(shift_register_3_q31[21]), .q11(shift_register_3_q31[20]), .q12(shift_register_3_q31[19]),
    .q13(shift_register_3_q31[18]), .q14(shift_register_3_q31[17]), .q15(shift_register_3_q31[16]),
    .q16(shift_register_3_q31[15]), .q17(shift_register_3_q31[14]), .q18(shift_register_3_q31[13]),
    .q19(shift_register_3_q31[12]), .q20(shift_register_3_q31[11]), .q21(shift_register_3_q31[10]),
    .q22(shift_register_3_q31[9]), .q23(shift_register_3_q31[8]), .q24(shift_register_3_q31[7]),
    .q25(shift_register_3_q31[6]), .q26(shift_register_3_q31[5]), .q27(shift_register_3_q31[4]),
    .q28(shift_register_3_q31[3]), .q29(shift_register_3_q31[2]), .q30(shift_register_3_q31[1]),
    .q31(shift_register_3_q31[0]));  // open: out, load, clr, d0, d1, d2, d3, d4, d5, d6, d7, d8, d9, d10, d11, d12, d13, d14, d15, d16, d17, d18, d19, d20, d21, d22, d23, d24, d25, d26, d27, d28, d29, d30, d31
  Shift_Register #(.length(32)) shift_register_4 (
    .shift(clock_1_out), .in(adder_6_out), .clk(clock_1_out), .q0(shift_register_4_q31[31]),
    .q1(shift_register_4_q31[30]), .q2(shift_register_4_q31[29]), .q3(shift_register_4_q31[28]),
    .q4(shift_register_4_q31[27]), .q5(shift_register_4_q31[26]), .q6(shift_register_4_q31[25]),
    .q7(shift_register_4_q31[24]), .q8(shift_register_4_q31[23]), .q9(shift_register_4_q31[22]),
    .q10(shift_register_4_q31[21]), .q11(shift_register_4_q31[20]), .q12(shift_register_4_q31[19]),
    .q13(shift_register_4_q31[18]), .q14(shift_register_4_q31[17]), .q15(shift_register_4_q31[16]),
    .q16(shift_register_4_q31[15]), .q17(shift_register_4_q31[14]), .q18(shift_register_4_q31[13]),
    .q19(shift_register_4_q31[12]), .q20(shift_register_4_q31[11]), .q21(shift_register_4_q31[10]),
    .q22(shift_register_4_q31[9]), .q23(shift_register_4_q31[8]), .q24(shift_register_4_q31[7]),
    .q25(shift_register_4_q31[6]), .q26(shift_register_4_q31[5]), .q27(shift_register_4_q31[4]),
    .q28(shift_register_4_q31[3]), .q29(shift_register_4_q31[2]), .q30(shift_register_4_q31[1]),
    .q31(shift_register_4_q31[0]));  // open: out, load, clr, d0, d1, d2, d3, d4, d5, d6, d7, d8, d9, d10, d11, d12, d13, d14, d15, d16, d17, d18, d19, d20, d21, d22, d23, d24, d25, d26, d27, d28, d29, d30, d31
  Shift_Register #(.length(32)) shift_register_5 (
    .shift(clock_1_out), .in(adder_7_out), .clk(clock_1_out), .q0(shift_register_5_q31[31]),
    .q1(shift_register_5_q31[30]), .q2(shift_register_5_q31[29]), .q3(shift_register_5_q31[28]),
    .q4(shift_register_5_q31[27]), .q5(shift_register_5_q31[26]), .q6(shift_register_5_q31[25]),
    .q7(shift_register_5_q31[24]), .q8(shift_register_5_q31[23]), .q9(shift_register_5_q31[22]),
    .q10(shift_register_5_q31[21]), .q11(shift_register_5_q31[20]), .q12(shift_register_5_q31[19]),
    .q13(shift_register_5_q31[18]), .q14(shift_register_5_q31[17]), .q15(shift_register_5_q31[16]),
    .q16(shift_register_5_q31[15]), .q17(shift_register_5_q31[14]), .q18(shift_register_5_q31[13]),
    .q19(shift_register_5_q31[12]), .q20(shift_register_5_q31[11]), .q21(shift_register_5_q31[10]),
    .q22(shift_register_5_q31[9]), .q23(shift_register_5_q31[8]), .q24(shift_register_5_q31[7]),
    .q25(shift_register_5_q31[6]), .q26(shift_register_5_q31[5]), .q27(shift_register_5_q31[4]),
    .q28(shift_register_5_q31[3]), .q29(shift_register_5_q31[2]), .q30(shift_register_5_q31[1]),
    .q31(shift_register_5_q31[0]));  // open: out, load, clr, d0, d1, d2, d3, d4, d5, d6, d7, d8, d9, d10, d11, d12, d13, d14, d15, d16, d17, d18, d19, d20, d21, d22, d23, d24, d25, d26, d27, d28, d29, d30, d31
  Counter #(.width(5), .max('h1f)) counter_2 (
    .Q(counter_2_q), .clk(counter_5_carry));  // open: load, D, count, carry, clr
  Counter #(.width(5), .max('h1f)) counter_3 (
    .Q(counter_3_q), .clk(counter_6_carry));  // open: load, D, count, carry, clr
  Counter #(.width(5), .max('h1f)) counter_4 (
    .Q(counter_4_q), .clk(counter_7_carry));  // open: load, D, count, carry, clr
  Counter #(.max('h1f)) counter_5 (.carry(counter_5_carry), .clk(clock_1_out));  // open: load, D, count, Q, clr
  Counter #(.max('h1f)) counter_6 (.carry(counter_6_carry), .clk(clock_1_out));  // open: load, D, count, Q, clr
  Counter #(.max('h1f)) counter_7 (.carry(counter_7_carry), .clk(clock_1_out));  // open: load, D, count, Q, clr
  RAM #(.addrWidth(5), .dataWidth(32)) ram_1 (
    .addr(counter_2_q), .data(ram_1_data), .clk(clock_1_out), .ld(counter_5_carry));  // open: sel, clr
  RAM #(.addrWidth(5), .dataWidth(32)) ram_2 (
    .addr(counter_3_q), .data(ram_2_data), .clk(clock_1_out), .ld(counter_6_carry));  // open: sel, clr
  RAM #(.addrWidth(5), .dataWidth(32)) ram_3 (
    .addr(counter_4_q), .data(ram_3_data), .clk(clock_1_out), .ld(counter_7_carry));  // open: sel, clr
  assign ram_1_data = 1'b1 ? shift_register_3_q31 : 32'bz;  // Controlled_Buffer controlled_buffer_1
  assign ram_2_data = 1'b1 ? shift_register_4_q31 : 32'bz;  // Controlled_Buffer controlled_buffer_2
  assign ram_3_data = 1'b1 ? shift_register_5_q31 : 32'bz;  // Controlled_Buffer controlled_buffer_3

  // Notes on the sheet:
  //   sattelite 1 prn code
  //   sattelite 2 prn code
  //   sat3
endmodule
